# Fritzing sketch RangeFinderXMit (saved by Fritzing 0.9.4)
breadboards: 1

parts:
  part = RF-LINK_TX [package=rf-link_tx]
  part_2 = Arduino Uno (Rev3)
  part_3 = HC-SR04 Ultrasonic Distance Sensor (Corrected)

nets:
  N1: part.DATA, part_2.D12/MISO
  GND: part.GND, part_2.GND, part_3.GND
  +5V: part.+5V, part_2.5V, part_3.VCC
  N2: part_2.D6_PWM, part_3.TRIG
  N3: part_2.D7, part_3.ECHO

custom parts:
  HC-SR04 Ultrasonic Distance Sensor (Corrected): The HC-SR04 is an ultrasonic distance sensor. It is capable of providing measurement for ranges of 2cm to 400cm. The module operates at 5V.
