# Fritzing sketch cable_tester (saved by Fritzing 0.9.4)
breadboards: 1

parts:
  U1 = 74HC595 [package="DIP16 [THT]"]
  Part1 = Arduino Uno (Rev3)
  S1 = Pushbutton [package="[THT]"]
  U2 = RJ45 Jack [package=rj45-8]
  U3 = RJ45 Jack [package=rj45-8]

nets:
  N1: U1.Q1, U2.2
  N2: U1.Q2, U2.3
  N3: U1.Q3, U2.4
  N4: U1.Q4, U2.5
  N5: U1.Q5, U2.6
  N6: U1.Q6, U2.7
  N7: U1.Q7, U2.8
  GND: U1.GND, U1.OE, Part1.GND, S1.Pin_3, S1.Pin_4
  VCC: U1.MR, U1.VCC, Part1.5V
  N8: U1.SH_CP, Part1.D13/SCK
  N9: U1.ST_CP, Part1.D12/MISO
  N10: U1.DS, Part1.D11_PWM/MOSI
  N11: U1.Q0, U2.1
  N12: Part1.A2, S1.Pin_1, S1.Pin_2
  N13: Part1.D8, U3.6
  N14: Part1.D9_PWM, U3.7
  N15: Part1.D10_PWM/SS, U3.8
  N16: Part1.D2, U3.1
  N17: Part1.D3_PWM, U3.2
  N18: Part1.D5_PWM, U3.3
  N19: Part1.D6_PWM, U3.4
  N20: Part1.D7, U3.5
